// Logisim project assign1bonus.circ as structural Verilog: 9 circuits, main circuit main
module main (
);

  wire button_1_out, Decoder_Circuitry_a, Decoder_Circuitry_b, Decoder_Circuitry_c, Decoder_Circuitry_d,
       Decoder_Circuitry_e, Decoder_Circuitry_f, Decoder_Circuitry_g;
  wire [3:0] counter_1_q;

  Counter #(.width(4), .max('hf)) counter_1 (.Q(counter_1_q), .clk(button_1_out));  // open: load, D, count, carry, clr
  Button button_1 (.out(button_1_out));
  Decoder_Circuitry Decoder_Circuitry (
    .w(counter_1_q[3]), .x(counter_1_q[2]), .y(counter_1_q[1]), .z(counter_1_q[0]), .A(Decoder_Circuitry_a),
    .B(Decoder_Circuitry_b), .C(Decoder_Circuitry_c), .D(Decoder_Circuitry_d), .E(Decoder_Circuitry_e),
    .G(Decoder_Circuitry_g), .F(Decoder_Circuitry_f));
  _7_Segment_Display u_7_segment_display_1 (
    .g(Decoder_Circuitry_g), .f(Decoder_Circuitry_f), .a(Decoder_Circuitry_a), .b(Decoder_Circuitry_b),
    .e(Decoder_Circuitry_e), .d(Decoder_Circuitry_d), .c(Decoder_Circuitry_c));  // open: dp
endmodule

module A (
  input  w,
  input  x,
  input  y,
  input  z,
  output out_5
);

  wire not_1_out, not_2_out, not_3_out, not_4_out, or_1_out, w_prime_x_z_out, w_prime_y_out,
       w_x_prime_y_prime_out, w_z_prime_out, x_prime_z_prime_out, x_y_out;

  not not_1 (not_1_out, x);
  not not_2 (not_2_out, w);
  not not_3 (not_3_out, y);
  not not_4 (not_4_out, z);
  and w_z_prime (w_z_prime_out, w, not_4_out);
  and x_prime_z_prime (x_prime_z_prime_out, not_1_out, not_4_out);
  and w_x_prime_y_prime (w_x_prime_y_prime_out, w, not_1_out, not_3_out);
  and w_prime_x_z (w_prime_x_z_out, not_2_out, x, z);
  and w_prime_y (w_prime_y_out, not_2_out, y);
  and x_y (x_y_out, x, y);
  or or_1 (or_1_out, w_z_prime_out, x_prime_z_prime_out, w_x_prime_y_prime_out, w_prime_x_z_out, w_prime_y_out);
  or or_2 (out_5, or_1_out, x_y_out);

  // Notes on the sheet:
  //   A
endmodule

module B (
  input  w,
  input  x,
  input  y,
  input  z,
  output out_5
);

  wire not_1_out, not_2_out, not_3_out, not_4_out, w_prime_x_prime_out, w_prime_y_prime_z_prime_out,
       w_prime_y_z_out, w_y_prime_z_out, x_prime_z_prime_out;

  not not_1 (not_1_out, x);
  not not_2 (not_2_out, w);
  not not_3 (not_3_out, y);
  not not_4 (not_4_out, z);
  and x_prime_z_prime (x_prime_z_prime_out, not_1_out, not_4_out);
  and w_prime_x_prime (w_prime_x_prime_out, not_2_out, not_1_out);
  and w_prime_y_prime_z_prime (w_prime_y_prime_z_prime_out, not_2_out, not_3_out, not_4_out);
  and w_prime_y_z (w_prime_y_z_out, not_2_out, y, z);
  and w_y_prime_z (w_y_prime_z_out, w, not_3_out, z);
  or or_1 (out_5, x_prime_z_prime_out, w_prime_x_prime_out, w_prime_y_prime_z_prime_out, w_prime_y_z_out, w_y_prime_z_out);

  // Notes on the sheet:
  //   B
endmodule

module C (
  input  w,
  input  x,
  input  y,
  input  z,
  output out_5
);

  wire not_1_out, not_2_out, not_3_out, w_prime_x_out, w_prime_y_prime_out, w_prime_z_out, w_x_prime_out,
       y_prime_z_out;

  not not_1 (not_1_out, x);
  not not_2 (not_2_out, w);
  not not_3 (not_3_out, y);
  and y_prime_z (y_prime_z_out, not_3_out, z);
  and w_x_prime (w_x_prime_out, w, not_1_out);
  and w_prime_x (w_prime_x_out, not_2_out, x);
  and w_prime_y_prime (w_prime_y_prime_out, not_2_out, not_3_out);
  and w_prime_z (w_prime_z_out, not_2_out, z);
  or or_1 (out_5, y_prime_z_out, w_x_prime_out, w_prime_x_out, w_prime_y_prime_out, w_prime_z_out);

  // Notes on the sheet:
  //   C
endmodule

module D (
  input  w,
  input  x,
  input  y,
  input  z,
  output out_5
);

  wire not_1_out, not_2_out, not_3_out, not_4_out, w_prime_x_prime_z_prime_out, w_y_prime_out,
       x_prime_y_z_out, x_y_prime_z_out, x_y_z_prime_out;

  not not_1 (not_1_out, w);
  not not_2 (not_2_out, x);
  not not_3 (not_3_out, y);
  not not_4 (not_4_out, z);
  and w_y_prime (w_y_prime_out, w, not_3_out);
  and x_prime_y_z (x_prime_y_z_out, not_2_out, y, z);
  and x_y_prime_z (x_y_prime_z_out, x, not_3_out, z);
  and w_prime_x_prime_z_prime (w_prime_x_prime_z_prime_out, not_1_out, not_2_out, not_4_out);
  and x_y_z_prime (x_y_z_prime_out, x, y, not_4_out);
  or or_1 (out_5, w_y_prime_out, x_prime_y_z_out, x_y_prime_z_out, w_prime_x_prime_z_prime_out, x_y_z_prime_out);

  // Notes on the sheet:
  //   D
endmodule

module E (
  input  w,
  input  x,
  input  y,
  input  z,
  output out_5
);

  wire not_1_out, not_2_out, w_x_out, w_y_out, x_prime_z_prime_out, y_z_prime_out;

  not not_1 (not_1_out, x);
  not not_2 (not_2_out, z);
  and x_prime_z_prime (x_prime_z_prime_out, not_1_out, not_2_out);
  and y_z_prime (y_z_prime_out, y, not_2_out);
  and w_x (w_x_out, w, x);
  and w_y (w_y_out, w, y);
  or or_1 (out_5, x_prime_z_prime_out, y_z_prime_out, w_x_out, w_y_out);

  // Notes on the sheet:
  //   E
endmodule

module F (
  input  w,
  input  x,
  input  y,
  input  z,
  output out_5
);

  wire not_1_out, not_2_out, not_3_out, not_4_out, w_prime_x_y_prime_out, w_x_prime_out, w_y_out,
       x_z_prime_out, y_prime_z_prime_out;

  not not_1 (not_1_out, w);
  not not_2 (not_2_out, x);
  not not_3 (not_3_out, y);
  not not_4 (not_4_out, z);
  and w_x_prime (w_x_prime_out, w, not_2_out);
  and x_z_prime (x_z_prime_out, x, not_4_out);
  and w_y (w_y_out, w, y);
  and y_prime_z_prime (y_prime_z_prime_out, not_3_out, not_4_out);
  and w_prime_x_y_prime (w_prime_x_y_prime_out, not_1_out, x, not_3_out);
  or or_1 (out_5, w_x_prime_out, x_z_prime_out, w_y_out, y_prime_z_prime_out, w_prime_x_y_prime_out);

  // Notes on the sheet:
  //   F
endmodule

module G (
  input  w,
  input  x,
  input  y,
  input  z,
  output out_5
);

  wire not_1_out, not_2_out, not_3_out, not_4_out, w_prime_x_y_prime_out, w_x_prime_out, w_z_out,
       x_prime_y_out, y_z_prime_out;

  not not_1 (not_1_out, w);
  not not_2 (not_2_out, x);
  not not_3 (not_3_out, y);
  not not_4 (not_4_out, z);
  and x_prime_y (x_prime_y_out, not_2_out, y);
  and w_x_prime (w_x_prime_out, w, not_2_out);
  and y_z_prime (y_z_prime_out, y, not_4_out);
  and w_z (w_z_out, w, z);
  and w_prime_x_y_prime (w_prime_x_y_prime_out, not_1_out, x, not_3_out, not_3_out);
  or or_1 (out_5, x_prime_y_out, w_x_prime_out, y_z_prime_out, w_z_out, w_prime_x_y_prime_out);

  // Notes on the sheet:
  //   G
endmodule

module Decoder_Circuitry (
  input  w,
  input  x,
  input  y,
  input  z,
  output A,
  output B,
  output C,
  output D,
  output E,
  output F,
  output G
);

  A u_A (.w(w), .x(x), .y(y), .z(z), .out_5(A));
  B u_B (.w(w), .x(x), .y(y), .z(z), .out_5(B));
  C u_C (.w(w), .x(x), .y(y), .z(z), .out_5(C));
  D u_D (.w(w), .x(x), .y(y), .z(z), .out_5(D));
  E u_E (.w(w), .x(x), .y(y), .z(z), .out_5(E));
  F u_F (.w(w), .x(x), .y(y), .z(z), .out_5(F));
  G u_G (.w(w), .x(x), .y(y), .z(z), .out_5(G));
endmodule
