// Logisim project assign2.circ as structural Verilog: 11 circuits, main circuit main
module main (
  input  in_1,
  input  in_2
);

  wire abc_1_out_3, abc_1_out_4, abc_1_out_5;

  ABC abc_1 (.D(in_1), .E(in_2), .out_3(abc_1_out_3), .out_4(abc_1_out_4), .out_5(abc_1_out_5));
  LED led_1 (.in(abc_1_out_3));
  LED led_2 (.in(abc_1_out_4));
  LED led_3 (.in(abc_1_out_5));
endmodule

module JA (
  input  B,
  input  C,
  input  D,
  input  E,
  output Ja
);

  wire B_prime_C_prime_DE_out, BC_prime_D_prime_E_out, not_1_out, not_2_out, not_3_out;

  not not_1 (not_1_out, B);
  not not_2 (not_2_out, C);
  not not_3 (not_3_out, D);
  and BC_prime_D_prime_E (BC_prime_D_prime_E_out, B, not_2_out, not_3_out, E);
  and B_prime_C_prime_DE (B_prime_C_prime_DE_out, not_1_out, not_2_out, D, E);
  or or_1 (Ja, BC_prime_D_prime_E_out, B_prime_C_prime_DE_out);
endmodule

module KA (
  input  B,
  input  C,
  input  D,
  input  E,
  output Ka
);

  wire B_prime_C_prime_D_prime_E_out, BC_prime_DE_out, not_1_out, not_2_out, not_3_out;

  not not_1 (not_1_out, B);
  not not_2 (not_2_out, D);
  not not_3 (not_3_out, C);
  and B_prime_C_prime_D_prime_E (B_prime_C_prime_D_prime_E_out, not_1_out, not_3_out, not_2_out, E);
  and BC_prime_DE (BC_prime_DE_out, B, not_3_out, D, E);
  or or_1 (Ka, B_prime_C_prime_D_prime_E_out, BC_prime_DE_out);
endmodule

module JB (
  input  A,
  input  C,
  input  D,
  input  E,
  output Jb
);

  wire A_prime_BD_prime_E_out, ACDE_out, not_1_out, not_2_out;

  not not_1 (not_1_out, A);
  not not_2 (not_2_out, D);
  and A_prime_BD_prime_E (A_prime_BD_prime_E_out, not_1_out, C, not_2_out, E);
  and ACDE (ACDE_out, A, C, D, E);
  or or_1 (Jb, A_prime_BD_prime_E_out, ACDE_out);
endmodule

module KB (
  input  A,
  input  C,
  input  D,
  input  E,
  output Kb
);

  wire A_prime_CDE_out, ACD_prime_E_out, not_1_out, not_2_out;

  not not_1 (not_1_out, A);
  not not_2 (not_2_out, D);
  and A_prime_CDE (A_prime_CDE_out, not_1_out, C, D, E);
  and ACD_prime_E (ACD_prime_E_out, A, C, not_2_out, E);
  or or_1 (Kb, A_prime_CDE_out, ACD_prime_E_out);
endmodule

module JC (
  input  A,
  input  B,
  input  D,
  input  E,
  output Jc
);

  wire A_prime_B_prime_D_prime_E_out, A_prime_BDE_out, AB_prime_DE_out, ABD_prime_E_out, not_1_out,
       not_2_out, not_3_out;

  not not_1 (not_1_out, A);
  not not_2 (not_2_out, B);
  not not_3 (not_3_out, D);
  and A_prime_B_prime_D_prime_E (A_prime_B_prime_D_prime_E_out, not_1_out, not_2_out, not_3_out, E);
  and A_prime_BDE (A_prime_BDE_out, not_1_out, B, D, E);
  and ABD_prime_E (ABD_prime_E_out, A, B, not_3_out, E);
  and AB_prime_DE (AB_prime_DE_out, A, not_2_out, D, E);
  or or_1 (Jc, A_prime_B_prime_D_prime_E_out, A_prime_BDE_out, ABD_prime_E_out, AB_prime_DE_out);
endmodule

module KC (
  input  A,
  input  B,
  input  D,
  input  E,
  output Kc
);

  wire A_prime_B_prime_DE_out, A_prime_BD_prime_E_out, AB_prime_D_prime_E_out, ABDE_out, not_1_out,
       not_2_out, not_3_out;

  not not_1 (not_1_out, A);
  not not_2 (not_2_out, B);
  not not_3 (not_3_out, D);
  and A_prime_BD_prime_E (A_prime_BD_prime_E_out, not_1_out, B, not_3_out, E);
  and A_prime_B_prime_DE (A_prime_B_prime_DE_out, not_1_out, not_2_out, D, E);
  and AB_prime_D_prime_E (AB_prime_D_prime_E_out, A, not_2_out, not_3_out, E);
  and ABDE (ABDE_out, A, B, D, E);
  or or_1 (Kc, A_prime_BD_prime_E_out, A_prime_B_prime_DE_out, AB_prime_D_prime_E_out, ABDE_out);
endmodule

module JK_A (
  input  B,
  input  C,
  input  D,
  input  E,
  input  Clock,
  output out_6
);

  wire JA_ja, KA_ka;

  JA JA (.B(B), .C(C), .D(D), .E(E), .Ja(JA_ja));
  KA KA (.B(B), .C(C), .D(D), .E(E), .Ka(KA_ka));
  J_K_Flip_Flop j_k_ff_1 (.J(JA_ja), .clk(Clock), .K(KA_ka), .Q(out_6));  // open: Qn, preset, en, reset
endmodule

module JK_B (
  input  A,
  input  C,
  input  D,
  input  E,
  input  Clock,
  output out_6
);

  wire JB_jb, KB_kb;

  JB JB (.A(A), .C(C), .D(D), .E(E), .Jb(JB_jb));
  KB KB (.A(A), .C(C), .D(D), .E(E), .Kb(KB_kb));
  J_K_Flip_Flop j_k_ff_1 (.J(JB_jb), .clk(Clock), .K(KB_kb), .Q(out_6));  // open: Qn, preset, en, reset
endmodule

module JK_C (
  input  A,
  input  B,
  input  D,
  input  E,
  input  Clock,
  output out_6
);

  wire JC_jc, KC_kc;

  JC JC (.A(A), .B(B), .D(D), .E(E), .Jc(JC_jc));
  KC KC (.A(A), .B(B), .D(D), .E(E), .Kc(KC_kc));
  J_K_Flip_Flop j_k_ff_1 (.J(JC_jc), .clk(Clock), .K(KC_kc), .Q(out_6));  // open: Qn, preset, en, reset
endmodule

module ABC (
  input  D,
  input  E,
  output out_3,
  output out_4,
  output out_5
);

  wire clock_1_out;

  Clock clock_1 (.out(clock_1_out));
  JK_A JK_A (.B(out_4), .C(out_5), .D(D), .E(E), .Clock(clock_1_out), .out_6(out_3));
  JK_B JK_B (.A(out_3), .C(out_5), .D(D), .E(E), .Clock(clock_1_out), .out_6(out_4));
  JK_C JK_C (.A(out_3), .B(out_4), .D(D), .E(E), .Clock(clock_1_out), .out_6(out_5));

  // Other names for the same wires on the sheet: A = out_3; B = out_4; C = out_5
endmodule
