// Logisim project assign2bonus.circ as structural Verilog: 5 circuits, main circuit main
module main (
  input  D,
  input  E
);

  wire abc_1_out_3, abc_1_out_4, abc_1_out_5;

  ABC abc_1 (.D(D), .E(E), .out_3(abc_1_out_3), .out_4(abc_1_out_4), .out_5(abc_1_out_5));
  LED led_1 (.in(abc_1_out_3));
  LED led_2 (.in(abc_1_out_4));
  LED led_3 (.in(abc_1_out_5));
endmodule

module TA (
  input  A,
  input  B,
  input  C,
  input  D,
  input  E,
  input  CLOCK,
  output TA
);

  wire A_prime_B_prime_C_prime_DE_out, A_prime_BC_prime_D_prime_E_out, AB_prime_C_prime_D_prime_E_out,
       ABC_prime_DE_out, not_1_out, not_2_out, not_3_out, not_4_out, or_1_out;

  not not_1 (not_1_out, A);
  not not_2 (not_2_out, B);
  not not_3 (not_3_out, C);
  not not_4 (not_4_out, D);
  and A_prime_BC_prime_D_prime_E (A_prime_BC_prime_D_prime_E_out, not_1_out, B, not_3_out, not_4_out, E);
  and A_prime_B_prime_C_prime_DE (A_prime_B_prime_C_prime_DE_out, not_1_out, not_2_out, not_3_out, D, E);
  and AB_prime_C_prime_D_prime_E (AB_prime_C_prime_D_prime_E_out, A, not_2_out, not_3_out, not_4_out, E);
  and ABC_prime_DE (ABC_prime_DE_out, A, B, not_3_out, D, E);
  or or_1 (or_1_out, A_prime_BC_prime_D_prime_E_out, A_prime_B_prime_C_prime_DE_out, AB_prime_C_prime_D_prime_E_out, ABC_prime_DE_out);
  T_Flip_Flop t_ff_1 (.clk(CLOCK), .T(or_1_out), .Q(TA));  // open: Qn, preset, reset, en
endmodule

module TB (
  input  A,
  input  B,
  input  C,
  input  D,
  input  E,
  input  CLOCK,
  output TB
);

  wire A_prime_B_prime_CD_prime_E_out, A_prime_BCDE_out, AB_prime_CDE_out, ABCD_prime_E_out, not_1_out,
       not_2_out, not_4_out, or_1_out;

  not not_1 (not_1_out, A);
  not not_2 (not_2_out, B);
  // NOT_Gate not_3 has open pins: in=C, out=open
  not not_4 (not_4_out, D);
  and A_prime_B_prime_CD_prime_E (A_prime_B_prime_CD_prime_E_out, not_1_out, not_2_out, C, not_4_out, E);
  and A_prime_BCDE (A_prime_BCDE_out, not_1_out, B, C, D, E);
  and ABCD_prime_E (ABCD_prime_E_out, A, B, C, not_4_out, E);
  and AB_prime_CDE (AB_prime_CDE_out, A, not_2_out, C, D, E);
  or or_1 (or_1_out, A_prime_B_prime_CD_prime_E_out, A_prime_BCDE_out, ABCD_prime_E_out, AB_prime_CDE_out);
  T_Flip_Flop t_ff_1 (.clk(CLOCK), .T(or_1_out), .Q(TB));  // open: Qn, preset, reset, en
endmodule

module TC (
  input  A,
  input  B,
  input  C,
  input  D,
  input  E,
  input  CLOCK,
  output TC
);

  wire A_prime_B_prime_C_prime_D_prime_E_out, A_prime_B_prime_CDE_out, A_prime_BC_prime_DE_out,
       A_prime_BCD_prime_E_out, AB_prime_C_prime_DE_out, AB_prime_CD_prime_E_out, ABC_prime_D_prime_E_out,
       ABCDE_out, not_1_out, not_2_out, not_3_out, not_4_out, or_1_out;

  not not_1 (not_1_out, A);
  not not_2 (not_2_out, C);
  not not_3 (not_3_out, B);
  not not_4 (not_4_out, D);
  and A_prime_B_prime_C_prime_D_prime_E (A_prime_B_prime_C_prime_D_prime_E_out, not_1_out, not_3_out, not_2_out, not_4_out, E);
  and A_prime_BCD_prime_E (A_prime_BCD_prime_E_out, not_1_out, B, C, not_4_out, E);
  and A_prime_B_prime_CDE (A_prime_B_prime_CDE_out, not_1_out, not_3_out, C, D, E);
  and A_prime_BC_prime_DE (A_prime_BC_prime_DE_out, not_1_out, B, not_2_out, D, E);
  and AB_prime_CD_prime_E (AB_prime_CD_prime_E_out, A, not_3_out, C, not_4_out, E);
  and ABC_prime_D_prime_E (ABC_prime_D_prime_E_out, A, B, not_2_out, not_4_out, E);
  and AB_prime_C_prime_DE (AB_prime_C_prime_DE_out, A, not_3_out, not_2_out, D, E);
  and ABCDE (ABCDE_out, A, B, C, D, E);
  or or_1 (or_1_out, A_prime_B_prime_C_prime_D_prime_E_out, A_prime_BCD_prime_E_out, A_prime_B_prime_CDE_out, A_prime_BC_prime_DE_out, AB_prime_CD_prime_E_out, ABC_prime_D_prime_E_out, AB_prime_C_prime_DE_out, ABCDE_out);
  T_Flip_Flop t_ff_1 (.clk(CLOCK), .T(or_1_out), .Q(TC));  // open: Qn, preset, reset, en
endmodule

module ABC (
  input  D,
  input  E,
  output out_3,
  output out_4,
  output out_5
);

  wire clock_1_out;

  Clock clock_1 (.out(clock_1_out));
  TA ta_1 (.A(out_3), .B(out_4), .C(out_5), .D(D), .E(E), .CLOCK(clock_1_out), .TA(out_3));
  TB tb_1 (.A(out_3), .B(out_4), .C(out_5), .D(D), .E(E), .CLOCK(clock_1_out), .TB(out_4));
  TC tc_1 (.A(out_3), .B(out_4), .C(out_5), .D(D), .E(E), .CLOCK(clock_1_out), .TC(out_5));

  // Other names for the same wires on the sheet: A = out_3; B = out_4; C = out_5
endmodule
